# Fritzing sketch CancelloGruppo11 (saved by Fritzing 0.9.3b)
breadboards: 2

parts:
  J2 = STM32 Nucleo boards
  S2 = KY-033 Tracing Black White Line Hunting Sensor Module For Arduino
  B3 = KY-004 Key Switch Module [package="Breakout board"]
  LED4 = LED - 5mm [color="Red (633nm)" package="5 mm [THT]"]
  LED5 = LED - 5mm [color="Yellow (595nm)" package="5 mm [THT]"]
  R4 = Resistor [tolerance=±5% resistance=220 package="0402 [SMD]"]
  R5 = Resistor [tolerance=±5% resistance=220 package="0402 [SMD]"]
  R6 = Resistor [tolerance=±5% resistance=220 package="0402 [SMD]"]
  S1 = KY-033 Tracing Black White Line Hunting Sensor Module For Arduino
  B2 = KY-004 Key Switch Module [package="Breakout board"]
  B1 = KY-004 Key Switch Module [package="Breakout board"]
  LED6 = LED - 3mm [color="Green (555nm)" package="3 mm [THT]"]

nets:
  N1: J2.PC11, S2.S
  GND: J2.GND#333, S2.GND, B3.-, S1.GND, B2.-, B1.-
  VIN: J2.5V, S2.V+, B3.Vin, S1.V+, B2.Vin, B1.Vin
  N2: J2.GND#2223, LED4.cathode, LED5.cathode, LED6.cathode
  N3: J2.PB4, R6.Pin_0
  N4: J2.PB5, R5.Pin_0
  N5: J2.PB3, R4.Pin_0
  N6: J2.PC1, B1.S
  N7: J2.PC10, S1.S
  N8: J2.PC2, B2.S
  N9: J2.PC3, B3.S
  N10: LED4.anode, R5.Pin_1
  N11: LED5.anode, R6.Pin_1
  N12: R4.Pin_1, LED6.anode

custom parts:
  KY-033 Tracing Black White Line Hunting Sensor Module For Arduino: Tracing Black White Line Hunting Sensor Module For Arduino Description: This is KY-033 tracking sensor. The KY-033 measures the intensity of infrared radiation and delivers it as an analog output voltage. Features: Operating voltage: 2.5 - 12V(cannot over12V) working current: 18mA-20mA at 5V Enhanced accuracy Documents: http://www.vishay.com/docs/83760/tcrt5000.pdf
  KY-004 Key Switch Module: Arduino Key Switch Module Keyes KY-004 is a push button that will output a high signal when pressed.
